// Logisim project 8 bit-computer final version.circ as structural Verilog: 8 circuits, main circuit main
// 0x6
module main (
  input  [7:0] Testing_Data,
  input  OE_Testing_data,
  input  Instruction_Reg,
  input  Count_Enable,
  output [7:0] out_5,
  output [3:0] out_6,
  output [3:0] out_7,
  output [7:0] out_8,
  output [7:0] out_9,
  output [2:0] out_10,
  output [7:0] out_11,
  output [7:0] out_12,
  output [3:0] out_13,
  output [7:0] out_14,
  output [7:0] out_15
);

  wire C0, C1, C2, C3, C4, C5, C6, C7, C8, C9, C10, C11, C12, C13, C14, C15, clock_1_out, clock_2_out,
       clock_3_out, clock_4_out;
  wire [3:0] controlled_buffer_1_out, decimal_decoder_4_dout, decimal_decoder_4_dout_2,
       decimal_decoder_4_dout_3, decimal_decoder_4_dout_5, decimal_decoder_4_dout_6,
       decimal_decoder_4_dout_7, memory_address_1_dout;
  wire [7:0] bit_extender_1_out, bit_extender_2_out, register_1_dout;
  wire [31:0] decimal_decoder_1_dout, decimal_decoder_2_dout, decimal_decoder_3_dout, decimal_decoder_5_dout;
  wire [31:12] decimal_decoder_4_dout_4;

  Clock clock_1 (.out(clock_1_out));
  assign bit_extender_1_out = {{4{1'b0}}, out_7};  // Bit_Extender bit_extender_1
  Counter #(.width(4), .max('h2)) counter_1 (
    .D(controlled_buffer_1_out), .count(C0), .Q(out_7), .clk(clock_1_out), .clr(Instruction_Reg));  // open: load, carry
  Register register_1 (
    .Clock(clock_1_out), .WE(C7), .OE(C8), .Din(out_5), .Dout(register_1_dout), .Stored_Data(out_8));  // open: Reset
  Decimal_Decoder decimal_decoder_1 (.Din(out_11), .Dout(decimal_decoder_1_dout));
  Register register_2 (.Clock(clock_1_out), .WE(C12), .Din(out_5), .Stored_Data(out_11));  // open: OE, Reset, Dout
  ALU alu_1 (.Reg_A(out_11), .Reg_B(out_15), .OE(C11), .Dout(out_5), .ALU_Result(out_14));  // open: Carry_out
  Register Reg_B (.Clock(clock_1_out), .WE(C13), .Din(out_5), .Stored_Data(out_15));  // open: OE, Reset, Dout
  Decimal_Decoder decimal_decoder_2 (.Din(out_15), .Dout(decimal_decoder_2_dout));
  Decimal_Decoder decimal_decoder_3 (.Din(bit_extender_1_out), .Dout(decimal_decoder_3_dout));
  assign controlled_buffer_1_out = C1 ? out_7 : 4'bz;  // Controlled_Buffer controlled_buffer_1
  _7_Segment_Display u_7_segment_display_1 (
    .g(decimal_decoder_1_dout[11]), .f(decimal_decoder_1_dout[10]), .a(decimal_decoder_1_dout[9]),
    .b(decimal_decoder_1_dout[8]), .e(decimal_decoder_1_dout[27]), .d(decimal_decoder_1_dout[26]),
    .c(decimal_decoder_1_dout[25]), .dp(decimal_decoder_1_dout[24]));
  _7_Segment_Display u_7_segment_display_2 (
    .g(decimal_decoder_1_dout[15]), .f(decimal_decoder_1_dout[14]), .a(decimal_decoder_1_dout[13]),
    .b(decimal_decoder_1_dout[12]), .e(decimal_decoder_1_dout[31]), .d(decimal_decoder_1_dout[30]),
    .c(decimal_decoder_1_dout[29]), .dp(decimal_decoder_1_dout[28]));
  _7_Segment_Display u_7_segment_display_3 (
    .g(decimal_decoder_2_dout[11]), .f(decimal_decoder_2_dout[10]), .a(decimal_decoder_2_dout[9]),
    .b(decimal_decoder_2_dout[8]), .e(decimal_decoder_2_dout[27]), .d(decimal_decoder_2_dout[26]),
    .c(decimal_decoder_2_dout[25]), .dp(decimal_decoder_2_dout[24]));
  _7_Segment_Display u_7_segment_display_4 (
    .g(decimal_decoder_2_dout[15]), .f(decimal_decoder_2_dout[14]), .a(decimal_decoder_2_dout[13]),
    .b(decimal_decoder_2_dout[12]), .e(decimal_decoder_2_dout[31]), .d(decimal_decoder_2_dout[30]),
    .c(decimal_decoder_2_dout[29]), .dp(decimal_decoder_2_dout[28]));
  _7_Segment_Display u_7_segment_display_5 (
    .g(decimal_decoder_3_dout[7]), .f(decimal_decoder_3_dout[6]), .a(decimal_decoder_3_dout[5]),
    .b(decimal_decoder_3_dout[4]), .e(decimal_decoder_3_dout[23]), .d(decimal_decoder_3_dout[22]),
    .c(decimal_decoder_3_dout[21]), .dp(decimal_decoder_3_dout[20]));
  _7_Segment_Display u_7_segment_display_6 (
    .g(decimal_decoder_1_dout[7]), .f(decimal_decoder_1_dout[6]), .a(decimal_decoder_1_dout[5]),
    .b(decimal_decoder_1_dout[4]), .e(decimal_decoder_1_dout[23]), .d(decimal_decoder_1_dout[22]),
    .c(decimal_decoder_1_dout[21]), .dp(decimal_decoder_1_dout[20]));
  _7_Segment_Display u_7_segment_display_7 (
    .g(decimal_decoder_1_dout[3]), .f(decimal_decoder_1_dout[2]), .a(decimal_decoder_1_dout[1]),
    .b(decimal_decoder_1_dout[0]), .e(decimal_decoder_1_dout[19]), .d(decimal_decoder_1_dout[18]),
    .c(decimal_decoder_1_dout[17]), .dp(decimal_decoder_1_dout[16]));
  _7_Segment_Display u_7_segment_display_8 (
    .g(decimal_decoder_2_dout[3]), .f(decimal_decoder_2_dout[2]), .a(decimal_decoder_2_dout[1]),
    .b(decimal_decoder_2_dout[0]), .e(decimal_decoder_2_dout[19]), .d(decimal_decoder_2_dout[18]),
    .c(decimal_decoder_2_dout[17]), .dp(decimal_decoder_2_dout[16]));
  _7_Segment_Display u_7_segment_display_9 (
    .g(decimal_decoder_2_dout[7]), .f(decimal_decoder_2_dout[6]), .a(decimal_decoder_2_dout[5]),
    .b(decimal_decoder_2_dout[4]), .e(decimal_decoder_2_dout[23]), .d(decimal_decoder_2_dout[22]),
    .c(decimal_decoder_2_dout[21]), .dp(decimal_decoder_2_dout[20]));
  _7_Segment_Display u_7_segment_display_10 (
    .g(decimal_decoder_3_dout[3]), .f(decimal_decoder_3_dout[2]), .a(decimal_decoder_3_dout[1]),
    .b(decimal_decoder_3_dout[0]), .e(decimal_decoder_3_dout[19]), .d(decimal_decoder_3_dout[18]),
    .c(decimal_decoder_3_dout[17]), .dp(decimal_decoder_3_dout[16]));
  BitSelector #(.group(4)) bitselector_1 (.in(register_1_dout), .out(controlled_buffer_1_out), .sel(1'b0));
  LED D7 (.in(out_5[7]));
  assign out_5 = OE_Testing_data ? Testing_Data : 8'bz;  // Controlled_Buffer controlled_buffer_2
  LED D4 (.in(out_5[4]));
  LED D5 (.in(out_5[5]));
  LED D6 (.in(out_5[6]));
  LED D3 (.in(out_5[3]));
  LED D1 (.in(out_5[1]));
  LED D2 (.in(out_5[2]));
  LED D0 (.in(out_5[0]));
  assign out_5 = C5 ? out_9 : 8'bz;  // Controlled_Buffer controlled_buffer_3
  Clock clock_2 (.out(clock_2_out));
  Decimal_Decoder decimal_decoder_4 (
    .Din(out_12),
    .Dout({decimal_decoder_4_dout_4[31:28], decimal_decoder_4_dout_7, decimal_decoder_4_dout_6, decimal_decoder_4_dout_5, decimal_decoder_4_dout_4[15:12], decimal_decoder_4_dout_3, decimal_decoder_4_dout_2, decimal_decoder_4_dout}));
  Memory_Address memory_address_1 (
    .Clock(clock_2_out), .WE(C9), .OE(C10), .Din(controlled_buffer_1_out), .Dout(memory_address_1_dout),
    .Stored_Data(out_6));  // open: Reset
  Register register_3 (
    .Clock(clock_2_out), .WE(C4), .OE(C6), .Din(out_5), .Dout(out_5), .Stored_Data(out_9));  // open: Reset
  Register register_4 (
    .Clock(clock_2_out), .WE(C15), .OE(C14), .Din(out_5), .Dout(out_5), .Stored_Data(out_12));  // open: Reset
  _7_Segment_Display u_7_segment_display_11 (
    .g(decimal_decoder_4_dout_4[15]), .f(decimal_decoder_4_dout_4[14]), .a(decimal_decoder_4_dout_4[13]),
    .b(decimal_decoder_4_dout_4[12]), .e(decimal_decoder_4_dout_4[31]), .d(decimal_decoder_4_dout_4[30]),
    .c(decimal_decoder_4_dout_4[29]), .dp(decimal_decoder_4_dout_4[28]));
  _7_Segment_Display u_7_segment_display_12 (
    .g(decimal_decoder_4_dout_3[3]), .f(decimal_decoder_4_dout_3[2]), .a(decimal_decoder_4_dout_3[1]),
    .b(decimal_decoder_4_dout_3[0]), .e(decimal_decoder_4_dout_7[3]), .d(decimal_decoder_4_dout_7[2]),
    .c(decimal_decoder_4_dout_7[1]), .dp(decimal_decoder_4_dout_7[0]));
  _7_Segment_Display u_7_segment_display_13 (
    .g(decimal_decoder_4_dout[3]), .f(decimal_decoder_4_dout[2]), .a(decimal_decoder_4_dout[1]),
    .b(decimal_decoder_4_dout[0]), .e(decimal_decoder_4_dout_5[3]), .d(decimal_decoder_4_dout_5[2]),
    .c(decimal_decoder_4_dout_5[1]), .dp(decimal_decoder_4_dout_5[0]));
  _7_Segment_Display u_7_segment_display_14 (
    .g(decimal_decoder_4_dout_2[3]), .f(decimal_decoder_4_dout_2[2]), .a(decimal_decoder_4_dout_2[1]),
    .b(decimal_decoder_4_dout_2[0]), .e(decimal_decoder_4_dout_6[3]), .d(decimal_decoder_4_dout_6[2]),
    .c(decimal_decoder_4_dout_6[1]), .dp(decimal_decoder_4_dout_6[0]));
  LED D6_2 (.in(out_5[6]));
  LED D7_2 (.in(out_5[7]));
  LED D2_2 (.in(out_5[2]));
  LED D5_2 (.in(out_5[5]));
  LED D3_2 (.in(out_5[3]));
  LED D4_2 (.in(out_5[4]));
  LED D1_2 (.in(out_5[1]));
  LED D0_2 (.in(out_5[0]));
  Clock clock_3 (.out(clock_3_out));
  Counter #(.width(3), .max('h6)) counter_2 (
    .count(Count_Enable), .Q(out_10), .clk(clock_4_out));  // open: load, D, carry, clr
  Clock clock_4 (.out(clock_4_out));
  BitSelector #(.group(4)) bitselector_2 (.in(out_8), .out(out_13), .sel(1'b0));
  RAM #(.addrWidth(4), .bus("separate")) ram_1 (
    .addr(memory_address_1_dout), .din(out_5), .data(out_5), .str(C2), .clk(clock_3_out), .ld(C3));  // open: sel, clr
  assign bit_extender_2_out = {{5{1'b0}}, out_10};  // Bit_Extender bit_extender_2
  CU_1 cu_1_1 (
    .OPC0(out_13[0]), .OPC1(out_13[1]), .OPC2(out_13[2]), .OPC3(out_13[3]), .SC0(out_10[0]), .SC1(out_10[1]),
    .SC2(out_10[2]), .C0(C0), .C1(C1), .C2(C2), .C3(C3), .C4(C4), .C5(C5), .C6(C6), .C7(C7), .C8(C8),
    .C9(C9), .C10(C10), .C11(C11));
  CU_2 cu_2_1 (
    .OPC0(out_13[0]), .OPC1(out_13[1]), .OPC2(out_13[2]), .OPC3(out_13[3]), .SC0(out_10[0]), .SC1(out_10[1]),
    .SC2(out_10[2]), .C12(C12), .C13(C13), .C14(C14), .C15(C15));
  _7_Segment_Display u_7_segment_display_15 (
    .g(decimal_decoder_5_dout[3]), .f(decimal_decoder_5_dout[2]), .a(decimal_decoder_5_dout[1]),
    .b(decimal_decoder_5_dout[0]), .e(decimal_decoder_5_dout[19]), .d(decimal_decoder_5_dout[18]),
    .c(decimal_decoder_5_dout[17]), .dp(decimal_decoder_5_dout[16]));
  Decimal_Decoder decimal_decoder_5 (.Din(bit_extender_2_out), .Dout(decimal_decoder_5_dout));

  // Other names for the same wires on the sheet: OPCode[7:0] = out_8

  // Notes on the sheet:
  //   PC
  //   Reg A
  //   ALU
  //   PC DEC Value
  //   Internal Address Bus (4 bits)
  //   Internal Data Bus
  //   PC is like the generator of the opcode
  //   MBR stores the values that the Mar points at
  //   Very important Notes:
  //   MAR
  //   MBR
  //   Output Register
  //   Mar works like a pointer that point at the memory's addresses that the Pc gives it to the MAR
  //   Instruction register stores the OPCode that the CU use to perform instructions
  //   External Address Bus(4 bits)
  //   Eternal Data Bus
  //   Step Counter
  //   ٍٍStep Counter DEC Value
endmodule

module Memory_Cell (
  input  Clock,
  input  WE,
  input  Din,
  input  OE,
  input  Reset,
  output Dout,
  output Stored_Data
);

  wire and_1_out, and_2_out, not_1_out, or_1_out;

  not not_1 (not_1_out, WE);
  and and_1 (and_1_out, Stored_Data, not_1_out);
  and and_2 (and_2_out, WE, Din);
  or or_1 (or_1_out, and_1_out, and_2_out);
  D_Flip_Flop d_ff_1 (.clk(Clock), .D(or_1_out), .Q(Stored_Data), .reset(Reset));  // open: Qn, preset, en
  assign Dout = OE ? Stored_Data : 1'bz;  // Controlled_Buffer controlled_buffer_1
endmodule

module Register (
  input  Clock,
  input  WE,
  input  OE,
  input  Reset,
  input  [7:0] Din,
  output [7:0] Dout,
  output [7:0] Stored_Data
);

  Memory_Cell memory_cell_1 (
    .Clock(Clock), .WE(WE), .Din(Din[0]), .OE(OE), .Reset(Reset), .Dout(Dout[0]), .Stored_Data(Stored_Data[0]));
  Memory_Cell memory_cell_2 (
    .Clock(Clock), .WE(WE), .Din(Din[1]), .OE(OE), .Reset(Reset), .Dout(Dout[1]), .Stored_Data(Stored_Data[1]));
  Memory_Cell memory_cell_3 (
    .Clock(Clock), .WE(WE), .Din(Din[2]), .OE(OE), .Reset(Reset), .Dout(Dout[2]), .Stored_Data(Stored_Data[2]));
  Memory_Cell memory_cell_4 (
    .Clock(Clock), .WE(WE), .Din(Din[3]), .OE(OE), .Reset(Reset), .Dout(Dout[3]), .Stored_Data(Stored_Data[3]));
  Memory_Cell memory_cell_5 (
    .Clock(Clock), .WE(WE), .Din(Din[4]), .OE(OE), .Reset(Reset), .Dout(Dout[4]), .Stored_Data(Stored_Data[4]));
  Memory_Cell memory_cell_6 (
    .Clock(Clock), .WE(WE), .Din(Din[5]), .OE(OE), .Reset(Reset), .Dout(Dout[5]), .Stored_Data(Stored_Data[5]));
  Memory_Cell memory_cell_7 (
    .Clock(Clock), .WE(WE), .Din(Din[6]), .OE(OE), .Reset(Reset), .Dout(Dout[6]), .Stored_Data(Stored_Data[6]));
  Memory_Cell memory_cell_8 (
    .Clock(Clock), .WE(WE), .Din(Din[7]), .OE(OE), .Reset(Reset), .Dout(Dout[7]), .Stored_Data(Stored_Data[7]));

  // Other names for the same wires on the sheet: D0 = Din[0]; D1 = Din[1]; D2 = Din[2]; D3 = Din[3]; D4 = Din[4];
  //   D5 = Din[5]; D6 = Din[6]; D7 = Din[7]; SD0 = Stored_Data[0]; SD1 = Stored_Data[1]; SD2 = Stored_Data[2];
  //   SD3 = Stored_Data[3]; SD4 = Stored_Data[4]; SD5 = Stored_Data[5]; SD6 = Stored_Data[6]; SD7 = Stored_Data[7]
endmodule

module Memory_Address (
  input  Clock,
  input  WE,
  input  OE,
  input  Reset,
  input  [3:0] Din,
  output [3:0] Dout,
  output [3:0] Stored_Data
);

  Memory_Cell memory_cell_1 (
    .Clock(Clock), .WE(WE), .Din(Din[0]), .OE(OE), .Reset(Reset), .Dout(Dout[0]), .Stored_Data(Stored_Data[0]));
  Memory_Cell memory_cell_2 (
    .Clock(Clock), .WE(WE), .Din(Din[1]), .OE(OE), .Reset(Reset), .Dout(Dout[1]), .Stored_Data(Stored_Data[1]));
  Memory_Cell memory_cell_3 (
    .Clock(Clock), .WE(WE), .Din(Din[2]), .OE(OE), .Dout(Dout[2]), .Stored_Data(Stored_Data[2]));  // open: Reset
  Memory_Cell memory_cell_4 (
    .Clock(Clock), .WE(WE), .Din(Din[3]), .OE(OE), .Reset(Reset), .Dout(Dout[3]), .Stored_Data(Stored_Data[3]));

  // Other names for the same wires on the sheet: D0 = Din[0]; D1 = Din[1]; D2 = Din[2]; D3 = Din[3];
  //   SD0 = Stored_Data[0]; SD1 = Stored_Data[1]; SD2 = Stored_Data[2]; SD3 = Stored_Data[3]
endmodule

module ALU (
  input  [7:0] Reg_A,
  input  [7:0] Reg_B,
  input  OE,
  output [7:0] Dout,
  output [7:0] ALU_Result,
  output Carry_out
);

  Adder adder_1 (.a(Reg_A), .b(Reg_B), .out(ALU_Result), .cout(Carry_out));  // open: cin
  assign Dout = OE ? ALU_Result : 8'bz;  // Controlled_Buffer controlled_buffer_1
endmodule

module Decimal_Decoder (
  input  [7:0] Din,
  output [31:0] Dout
);

  ROM #(.dataWidth(32)) rom_1 (
    .addr(Din),
    .data({Dout[31:28], Dout[15:12], Dout[27:24], Dout[11:8], Dout[23:20], Dout[7:4], Dout[19:16], Dout[3:0]}));  // open: sel

  // Notes on the sheet:
  //   contents of rom_1 (hex, n*v repeats v):
  //   e7 21 cb 6b 2d 6e ee 23 ef 2f 21e7 2121 21cb 216b 212d 216e 21ee 2123 21ef 212f cbe7 cb21 cbcb cb6b
  //   cb2d cb6e cbee cb23 cbef cb2f 6be7 6b21 6bcb 6b6b 6b2d 6b6e 6bee 6b23 6bef 6b2f 2de7 2d21 2dcb 2d6b
  //   2d2d 2d6e 2dee 2d23 2def 2d2f 6ee7 6e21 6ecb 6e6b 6e2d 6e6e 6eee 6e23 6eef 6e2f eee7 ee21 eecb ee6b
  //   ee2d ee6e eeee ee23 eeef ee2f 23e7 2321 23cb 236b 232d 236e 23ee 2323 23ef 232f efe7 ef21 efcb ef6b
  //   ef2d ef6e efee ef23 efef ef2f 2fe7 2f21 2fcb 2f6b 2f2d 2f6e 2fee 2f23 2fef 2f2f 21e7e7 21e721 21e7cb
  //   21e76b 21e72d 21e76e 21e7ee 21e723 21e7ef 21e72f 2121e7 212121 2121cb 21216b 21212d 21216e 2121ee
  //   212123 2121ef 21212f 21cbe7 21cb21 21cbcb 21cb6b 21cb2d 21cb6e 21cbee 21cb23 21cbef 21cb2f 216be7
  //   216b21 216bcb 216b6b 216b2d 216b6e 216bee 216b23 216bef 216b2f 212de7 212d21 212dcb 212d6b 212d2d
  //   212d6e 212dee 212d23 212def 212d2f 216ee7 216e21 216ecb 216e6b 216e2d 216e6e 216eee 216e23 216eef
  //   216e2f 21eee7 21ee21 21eecb 21ee6b 21ee2d 21ee6e 21eeee 21ee23 21eeef 21ee2f 2123e7 212321 2123cb
  //   21236b 21232d 21236e 2123ee 212323 2123ef 21232f 21efe7 21ef21 21efcb 21ef6b 21ef2d 21ef6e 21efee
  //   21ef23 21efef 21ef2f 212fe7 212f21 212fcb 212f6b 212f2d 212f6e 212fee 212f23 212fef 212f2f cbe7e7
  //   cbe721 cbe7cb cbe76b cbe72d cbe76e cbe7ee cbe723 cbe7ef cbe72f cb21e7 cb2121 cb21cb cb216b cb212d
  //   cb216e cb21ee cb2123 cb21ef cb212f cbcbe7 cbcb21 cbcbcb cbcb6b cbcb2d cbcb6e cbcbee cbcb23 cbcbef
  //   cbcb2f cb6be7 cb6b21 cb6bcb cb6b6b cb6b2d cb6b6e cb6bee cb6b23 cb6bef cb6b2f cb2de7 cb2d21 cb2dcb
  //   cb2d6b cb2d2d cb2d6e cb2dee cb2d23 cb2def cb2d2f cb6ee7 cb6e21 cb6ecb cb6e6b cb6e2d cb6e6e
endmodule

module CU_1 (
  input  OPC0,
  input  OPC1,
  input  OPC2,
  input  OPC3,
  input  SC0,
  input  SC1,
  input  SC2,
  output C0,
  output C1,
  output C2,
  output C3,
  output C4,
  output C5,
  output C6,
  output C7,
  output C8,
  output C9,
  output C10,
  output C11
);

  wire and_1_out, and_2_out, and_3_out, and_4_out, and_5_out, and_6_out, and_7_out, and_8_out, and_9_out,
       and_12_out, and_13_out, and_14_out, and_15_out, and_16_out, and_17_out, and_18_out, not_1_out,
       not_2_out, not_3_out, not_4_out, not_5_out, not_6_out, not_7_out, not_8_out, not_9_out, not_10_out,
       not_11_out, not_12_out, not_13_out, not_14_out, not_15_out, not_16_out, not_17_out, not_18_out,
       not_19_out, not_20_out, not_21_out, not_22_out, not_23_out, not_24_out, not_25_out, not_26_out,
       not_27_out, not_28_out, not_29_out, not_30_out, not_31_out, not_32_out, not_33_out, not_34_out,
       not_35_out, not_36_out, not_37_out, not_38_out, not_39_out, not_40_out, not_41_out, not_42_out,
       not_43_out, not_44_out;

  not not_1 (not_1_out, OPC2);
  not not_2 (not_2_out, SC2);
  not not_3 (not_3_out, SC1);
  not not_4 (not_4_out, SC2);
  not not_5 (not_5_out, SC0);
  not not_6 (not_6_out, SC1);
  not not_7 (not_7_out, SC2);
  not not_8 (not_8_out, OPC2);
  not not_9 (not_9_out, SC2);
  not not_10 (not_10_out, SC1);
  not not_11 (not_11_out, SC2);
  not not_12 (not_12_out, SC0);
  not not_13 (not_13_out, SC1);
  not not_14 (not_14_out, OPC2);
  not not_15 (not_15_out, SC1);
  not not_16 (not_16_out, SC2);
  not not_17 (not_17_out, SC0);
  not not_18 (not_18_out, SC1);
  not not_19 (not_19_out, OPC2);
  not not_20 (not_20_out, SC1);
  not not_21 (not_21_out, SC2);
  not not_22 (not_22_out, OPC2);
  not not_23 (not_23_out, SC1);
  not not_24 (not_24_out, SC0);
  not not_25 (not_25_out, SC2);
  not not_26 (not_26_out, OPC2);
  not not_27 (not_27_out, SC0);
  not not_28 (not_28_out, SC0);
  not not_29 (not_29_out, SC1);
  not not_30 (not_30_out, SC2);
  not not_31 (not_31_out, SC0);
  not not_32 (not_32_out, SC1);
  not not_33 (not_33_out, SC2);
  not not_34 (not_34_out, OPC2);
  not not_35 (not_35_out, SC0);
  not not_36 (not_36_out, OPC3);
  not not_37 (not_37_out, SC0);
  not not_38 (not_38_out, SC1);
  not not_39 (not_39_out, OPC2);
  not not_40 (not_40_out, SC0);
  not not_41 (not_41_out, OPC2);
  not not_42 (not_42_out, SC1);
  not not_43 (not_43_out, SC2);
  not not_44 (not_44_out, SC0);
  and and_1 (and_1_out, not_1_out, SC0, SC1, not_2_out);
  and and_2 (and_2_out, OPC2, SC0, not_3_out, not_4_out);
  and and_3 (and_3_out, not_5_out, not_6_out, not_7_out);
  and and_4 (and_4_out, not_8_out, SC0, SC1, not_9_out);
  and and_5 (and_5_out, OPC2, not_10_out, not_11_out);
  and and_6 (and_6_out, not_12_out, not_13_out, SC2);
  and and_7 (and_7_out, not_14_out, SC0, not_15_out, not_16_out);
  and and_8 (and_8_out, not_17_out, not_18_out, SC2);
  and and_9 (and_9_out, not_19_out, SC0, not_20_out, not_21_out);
  and and_10 (C6, not_22_out, SC0, not_23_out, SC2);
  and and_11 (C7, not_24_out, SC1, not_25_out);
  and and_12 (and_12_out, not_26_out, not_27_out, SC1, SC2);
  and and_13 (and_13_out, OPC3, not_28_out, not_29_out, not_30_out);
  and and_14 (and_14_out, not_31_out, not_32_out, not_33_out);
  and and_15 (and_15_out, not_34_out, not_35_out, SC1, SC2);
  and and_16 (and_16_out, not_36_out, not_37_out, not_38_out);
  and and_17 (and_17_out, not_39_out, not_40_out, SC2);
  and and_18 (and_18_out, not_41_out, SC0, not_42_out, not_43_out);
  and and_19 (C11, OPC2, not_44_out, SC1, SC2);
  or or_1 (C0, and_1_out, and_2_out);
  or or_2 (C1, and_3_out, and_4_out, and_5_out);
  or or_3 (C3, and_6_out, and_7_out);
  or or_4 (C4, and_8_out, and_9_out);
  or or_5 (C8, and_12_out, and_13_out);
  or or_6 (C9, and_14_out, and_15_out);
  or or_7 (C10, and_16_out, and_17_out, and_18_out);

  assign C2 = 1'b0;
  assign C5 = 1'b0;
endmodule

module CU_2 (
  input  OPC0,
  input  OPC1,
  input  OPC2,
  input  OPC3,
  input  SC0,
  input  SC1,
  input  SC2,
  output C12,
  output C13,
  output C14,
  output C15
);

  wire not_1_out, not_2_out, not_3_out, not_4_out, not_5_out;

  not not_1 (not_1_out, OPC2);
  not not_2 (not_2_out, OPC3);
  not not_3 (not_3_out, SC1);
  not not_4 (not_4_out, SC1);
  not not_5 (not_5_out, SC0);
  and and_1 (C12, not_1_out, not_2_out, SC0, not_3_out, SC2);
  and and_2 (C13, OPC3, SC0, not_4_out, SC2);
  and and_3 (C15, OPC2, not_5_out, SC1, SC2);

  assign C14 = 1'b0;
endmodule
